# Fritzing sketch Reed_och_IR (saved by Fritzing 0.9.3b)
breadboards: 2

parts:
  LED1 = LED - 5mm [color="Red (633nm)" package="5 mm [THT]"]
  TX = LTE-302 [package=lte-302]
  RX = LTR-301 [package=ltr-301]
  Part1 = Arduino Uno (Rev3)
  R1 = Resistor [tolerance=±5% resistance=100 package=THT]
  R2 = Resistor [tolerance=±5% resistance=10k package=THT]
  R3 = Resistor [tolerance=±5% resistance=220 package=THT]
  S1 = Reed switch [package=THT]
  Q1 = NPN-Transistor [package="TO92 [THT]"]
  LED2 = LED - 5mm [color="Green (560nm)" package="5 mm [THT]"]
  R4 = Resistor [tolerance=±5% resistance=1k package=THT]
  R5 = Resistor [tolerance=±5% resistance=220 package=THT]

nets:
  N1: LED1.cathode, Q1.C
  N2: LED1.anode, Part1.D2, R3.Pin_0
  N3: TX.A, R1.Pin_0
  N4: TX.C, RX.C, Part1.GND, S1.pin_2, Q1.E, LED2.cathode
  N5: RX.E, R2.Pin_0, Q1.B
  N6: Part1.D4, S1.pin_1, R4.Pin_0
  N7: Part1.D7, R5.Pin_0
  N8: Part1.5V, R1.Pin_1, R2.Pin_1, R3.Pin_1, R4.Pin_1
  N9: LED2.anode, R5.Pin_1

// code stored in the sketch: reed_switch.ino
int LED = 7;
int reed_switch = 4;
int reed_status;

void setup() {
pinMode(LED, OUTPUT);
pinMode(reed_switch, INPUT);
}

void loop() {
reed_status = digitalRead(reed_switch);
if (reed_status == 1) digitalWrite(LED, LOW);
else digitalWrite(LED, HIGH);delay(1000);
}
